# Fritzing sketch pluto_prototype (saved by Fritzing 1.0.1rc)
breadboards: 1

parts:
  M1 = gear-motor
  M2 = gear-motor
  8-Channel_Relay1 = 8-Channel 5v Relay Shield [package=relay-8ch5v10a]
  M5 = MDD10A
  Mod3 = Raspberry Pi Pico
  Bauteil1 = Adafruit VL53L0X Time of Flight Distance Sensor [part_number="Adafruit #3317"]
  Bauteil2 = Adafruit VL53L0X Time of Flight Distance Sensor [part_number="Adafruit #3317"]
  Bauteil3 = Adafruit VL53L0X Time of Flight Distance Sensor [part_number="Adafruit #3317"]
  Bauteil4 = Adafruit VL53L0X Time of Flight Distance Sensor [part_number="Adafruit #3317"]
  Bauteil5 = MCP9808 High Accuracy I2C Temperature Sensor [part_number=1782]
  Bauteil6 = MCP9808 High Accuracy I2C Temperature Sensor [part_number=1782]
  A1 = NEO-6M GPS Module [part_number=GY-GPS6MV2]
  Module1 = Boladge HMC5883L Compass Module

nets:
  N1: M1.pin_1, M5.M1A1
  N2: M1.pin_2, M5.M1B-1
  N3: M2.pin_2, M5.M2A-1
  N4: 8-Channel_Relay1.VCC, Mod3.pin_40
  GND: 8-Channel_Relay1.GND, M5.Bat-, M5.GND, Mod3.pin_3, Mod3.pin_8, Mod3.pin_13, Mod3.pin_18, Mod3.pin_23, Mod3.pin_28, Mod3.pin_33, Mod3.pin_38, Bauteil1.GND, Bauteil2.GND, Bauteil3.GND, Bauteil4.GND, Bauteil5.GND, Bauteil6.GND, A1.GND, Module1.GND
  N5: 8-Channel_Relay1.IN1, Mod3.pin_12
  N6: 8-Channel_Relay1.IN2, Mod3.pin_11
  N7: M5.PWM2, Mod3.pin_20
  N8: M5.DIR2, Mod3.pin_16
  N9: M5.PWM1, Mod3.pin_19
  N10: M5.DIR1, Mod3.pin_15
  N11: Mod3.pin_1, A1.Tx
  N12: Mod3.pin_2, A1.Rx
  N13: Mod3.pin_21, Bauteil1.SDA, Bauteil2.SDA, Bauteil3.SDA, Bauteil4.SDA, Bauteil5.SDA, Bauteil6.SDA, Module1.SDA
  N14: Mod3.pin_22, Bauteil1.SCL, Bauteil2.SCL, Bauteil3.SCL, Bauteil4.SCL, Bauteil5.SCL, Bauteil6.SCL, Module1.SCL
  N15: Mod3.pin_24, Bauteil3.XSHUT
  N16: Mod3.pin_25, Bauteil3.GPIO
  N17: Mod3.pin_26, Bauteil2.GPIO
  N18: Mod3.pin_27, Bauteil2.XSHUT
  N19: Mod3.pin_29, Bauteil1.GPIO
  N20: Mod3.pin_30, Bauteil1.XSHUT
  VIN: Mod3.pin_37, Bauteil1.VIN, Bauteil2.VIN, Bauteil3.VIN, Bauteil4.VIN, Bauteil5.VDD, Bauteil6.VDD, Bauteil6.A1, A1.Vcc, Module1.VCC

notes:
  MCP9808-1 has address: 0x18
  MCP9808-2 has address: 0x1A (Pin A1 set to HIGH)

custom parts:
  8-Channel 5v Relay Shield: 8 Channel 5v Relay Shield w. 2x SPD-06VDC-SD-C
  Raspberry Pi Pico: Raspberry Pi Pico. Based around the RP2040 microcontroller the Pico is a low cost microcontroller device bringing Raspberry Pi quality, cost, and easy of use to the microcontroller space. Jan 2021, Split part in to two versions: tht (this one) and SMD. This one will drill holes for a .1 in header in pcb to allow plugging in the module as well as providing pads to solder the module to the top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
  Adafruit VL53L0X Time of Flight Distance Sensor: The VL53L0X is a Time of Flight distance sensor like no other you've used! The sensor contains a very tiny invisible laser source, and a matching sensor. The VL53L0X can detect the "time of flight", or how long the light has taken to bounce back to the sensor. Since it uses a very narrow light source, it is good for determining distance of only the surface directly in front of it. Unlike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
  MCP9808 High Accuracy I2C Temperature Sensor: This I2C digital temperature sensor is one of the more accurate/precise we've ever seen, with a typical accuracy of ±0.25°C over the sensor's -40°C to +125°C range and precision of +0.0625°C. They work great with any microcontroller using standard i2c. There are 3 address pins so you can connect up to 8 to a single I2C bus without address collisions. Best of all, a wide voltage range makes is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
  NEO-6M GPS Module: GY-GPS6MV2 NEO-6M GPS Module Module based on U-blox NEO-6M GPS engine, incorporating regulator for 3.3-5V DC input, MS621FE-compatible rechargeable battery for backup and EEPROM for storing configuration settings. Links: NEO-6 series product information page NEO-6 Datasheet
  Boladge HMC5883L Compass Module: Cheap digital compass module
